// Logisim project Decodificador 3x8.circ as structural Verilog: 2 circuits, main circuit main
module main (
);

  wire clock_1_out, dec_3x8_1_s0, dec_3x8_1_s1, dec_3x8_1_s2, dec_3x8_1_s3, dec_3x8_1_s4, dec_3x8_1_s5,
       dec_3x8_1_s6, dec_3x8_1_s7;
  wire [2:0] counter_1_q;

  Counter #(.width(3), .max('h7)) counter_1 (.Q(counter_1_q), .clk(clock_1_out));  // open: load, D, count, carry, clr
  Clock clock_1 (.out(clock_1_out));
  Dec_3x8 dec_3x8_1 (
    .S0(dec_3x8_1_s0), .S1(dec_3x8_1_s1), .S2(dec_3x8_1_s2), .S3(dec_3x8_1_s3), .S4(dec_3x8_1_s4),
    .S5(dec_3x8_1_s5), .S6(dec_3x8_1_s6), .S7(dec_3x8_1_s7), .ABC(counter_1_q));
  LED led_1 (.in(dec_3x8_1_s0));
  LED led_2 (.in(dec_3x8_1_s1));
  LED led_3 (.in(dec_3x8_1_s2));
  LED led_4 (.in(dec_3x8_1_s3));
  LED led_5 (.in(dec_3x8_1_s4));
  LED led_6 (.in(dec_3x8_1_s5));
  LED led_7 (.in(dec_3x8_1_s6));
  LED led_8 (.in(dec_3x8_1_s7));
endmodule

module Dec_3x8 (
  input  [2:0] ABC,
  output S0,
  output S1,
  output S2,
  output S3,
  output S4,
  output S5,
  output S6,
  output S7
);

  and and_1 (S0, ~ABC[2], ~ABC[1], ~ABC[0]);  // AND_Gate
  and and_2 (S1, ~ABC[2], ~ABC[1], ABC[0]);  // AND_Gate
  and and_3 (S2, ~ABC[2], ABC[1], ~ABC[0]);  // AND_Gate
  and and_4 (S3, ~ABC[2], ABC[1], ABC[0]);  // AND_Gate
  and and_5 (S4, ABC[2], ~ABC[1], ~ABC[0]);  // AND_Gate
  and and_6 (S5, ABC[2], ~ABC[1], ABC[0]);  // AND_Gate
  and and_7 (S6, ABC[2], ABC[1], ~ABC[0]);  // AND_Gate
  and and_8 (S7, ABC[2], ABC[1], ABC[0]);
endmodule
